// Logisim project 4bit_Adder_Subtractor.circ as structural Verilog: 2 circuits, main circuit main
module main (
  input  ADD___0__SUB___1,
  input  [3:0] A,
  input  [3:0] B,
  output [3:0] Result,
  output Z_zero,
  output N_sign,
  output V_overflow,
  output C_carry
);

  wire Bit_0_carry, Bit_1_carry, Bit_2_carry, xor_1_out, xor_2_out, xor_3_out, xor_4_out;

  xor xor_1 (xor_1_out, B[0], ADD___0__SUB___1);
  xor xor_2 (xor_2_out, B[1], ADD___0__SUB___1);
  xor xor_3 (xor_3_out, B[2], ADD___0__SUB___1);
  xor xor_4 (xor_4_out, B[3], ADD___0__SUB___1);
  FullAdder Bit_0 (.C(ADD___0__SUB___1), .A(A[0]), .B(xor_1_out), .Sum(Result[0]), .Carry(Bit_0_carry));
  FullAdder Bit_1 (.C(Bit_0_carry), .A(A[1]), .B(xor_2_out), .Sum(Result[1]), .Carry(Bit_1_carry));
  FullAdder Bit_2 (.C(Bit_1_carry), .A(A[2]), .B(xor_3_out), .Sum(Result[2]), .Carry(Bit_2_carry));
  FullAdder Bit_3 (.C(Bit_2_carry), .A(A[3]), .B(xor_4_out), .Sum(N_sign), .Carry(C_carry));
  nor nor_1 (Z_zero, N_sign, Result[2], Result[1], Result[0]);

  assign Result[3] = N_sign;
  assign V_overflow = C_carry;
endmodule

module FullAdder (
  input  C,
  input  A,
  input  B,
  output Sum,
  output Carry
);

  wire and_1_out, and_2_out, xor_1_out;

  xor xor_1 (xor_1_out, A, B);
  xor xor_2 (Sum, C, xor_1_out);
  and and_1 (and_1_out, C, xor_1_out);
  and and_2 (and_2_out, B, A);
  or or_1 (Carry, and_1_out, and_2_out);
endmodule
